# Fritzing sketch sema_spajanja (saved by Fritzing 0.9.3b)

parts:
  Mod1 = Raspberry Pi Pico W
  Rotacijski_enkoder = KY-040 Rotary encoder [package="Breakout board"]
  BMX055_Senzor = Triple Axis Accelerometer Breakout - ADXL345
  TFT1 = Color 320x240 TFT Display, ILI9341 Controller Chip
  R1 = Resistor [tolerance=±5% resistance=1k package="0805 [SMD]"]
  R2 = Resistor [tolerance=±5% resistance=1k package="0805 [SMD]"]
  R3 = Resistor [tolerance=±5% resistance=1k package="0805 [SMD]"]
  R4 = Resistor [tolerance=±5% resistance=1k package="0805 [SMD]"]
  R5 = Resistor [tolerance=±5% resistance=1k package="0805 [SMD]"]
  R6 = Resistor [tolerance=±5% resistance=1k package="0805 [SMD]"]
  R7 = Resistor [tolerance=±5% resistance=1k package="0805 [SMD]"]
  R8 = Resistor [tolerance=±5% resistance=1k package="0805 [SMD]"]
  LED8 = smd LED [color="Red (633nm)" package="0603 [SMD]"]
  LED9 = smd LED [color="Red (633nm)" package="0603 [SMD]"]
  LED10 = smd LED [color="Red (633nm)" package="0603 [SMD]"]
  LED13 = smd LED [color="Red (633nm)" package="0603 [SMD]"]
  LED14 = smd LED [color="Red (633nm)" package="0603 [SMD]"]
  LED15 = smd LED [color="Red (633nm)" package="0603 [SMD]"]
  LED16 = smd LED [color="Red (633nm)" package="0603 [SMD]"]
  S1 = Pushbutton [package="[THT]"]
  R9 = Resistor [tolerance=±5% resistance=1k package="0805 [SMD]"]
  LED6 = smd LED [color="Red (633nm)" package="0603 [SMD]"]

nets:
  N1: Mod1.pin_1, Rotacijski_enkoder.CLK
  N2: Mod1.pin_2, Rotacijski_enkoder.DT
  GND: Mod1.pin_3, Mod1.pin_23, Mod1.pin_33, Mod1.pin_38, Mod1.pin_42, Rotacijski_enkoder.GND, BMX055_Senzor.GND, TFT1.GND, LED8.cathode, LED9.cathode, LED10.cathode, LED13.cathode, LED14.cathode, LED15.cathode, LED16.cathode, R9.Pin_1, LED6.cathode
  N3: Mod1.pin_4, Rotacijski_enkoder.SW
  VCC: Mod1.pin_5, Mod1.pin_36, Rotacijski_enkoder.Vcc, BMX055_Senzor.VCC, TFT1.VCC, TFT1.LED, S1.Pin_3, S1.Pin_4, R9.Pin_0
  N4: Mod1.pin_6, R1.Pin_1
  N5: Mod1.pin_7, R2.Pin_1
  N6: Mod1.pin_9, R4.Pin_1
  N7: Mod1.pin_10, R3.Pin_1
  N8: Mod1.pin_11, R5.Pin_1
  N9: Mod1.pin_12, R6.Pin_1
  N10: Mod1.pin_14, R7.Pin_1
  N11: Mod1.pin_15, R8.Pin_1
  N12: Mod1.pin_20, TFT1.D/C
  N13: Mod1.pin_21, TFT1.SDI_(MOSI)
  N14: Mod1.pin_22, TFT1.CS
  N15: Mod1.pin_24, TFT1.SCK
  N16: Mod1.pin_25, TFT1.SDO_(MISO)
  N17: Mod1.pin_26, TFT1.Reset
  N18: Mod1.pin_31, BMX055_Senzor.SDA
  N19: Mod1.pin_32, BMX055_Senzor.SCL
  N20: R1.Pin_0, LED6.anode
  N21: R2.Pin_0, LED8.anode
  N22: R3.Pin_0, LED10.anode
  N23: R4.Pin_0, LED9.anode
  N24: R5.Pin_0, LED13.anode
  N25: R6.Pin_0, LED14.anode
  N26: R7.Pin_0, LED15.anode
  N27: R8.Pin_0, LED16.anode

custom parts:
  Raspberry Pi Pico W: Raspberry Pi Pico W. Based around the RP2040 microcontroller the Pico W is a low cost microcontroller device bringing Raspberry Pi quality, cost, and easy of use to the microcontroller space. The areas marked KEEPOUT in pcb silkscreen should not have traces running through them to avoid shorts on a soldered in module!
  KY-040 Rotary encoder: KY-040 Rotary Encoder with switch on breakout borad from AZ Delivery
  Color 320x240 TFT Display, ILI9341 Controller Chip: 2.2" TFT Display with ILI9341 Controller
