# Fritzing sketch sema (saved by Fritzing 0.9.3b)

parts:
  Mod1 = Raspberry Pi Pico W
  Rotacijski_enkoder = KY-040 Rotary encoder [package="Breakout board"]
  TFT_displej = TFT 1.8 inch 160x128 w SD
  BMX150_Senzor = Triple Axis Accelerometer Breakout - ADXL345

nets:
  N1: Mod1.pin_1, Rotacijski_enkoder.CLK
  N2: Mod1.pin_2, Rotacijski_enkoder.DT
  N3: Mod1.pin_3, Mod1.pin_23, Mod1.pin_33, Mod1.pin_42, Rotacijski_enkoder.GND, TFT_displej.pin2
  N4: Mod1.pin_4, Rotacijski_enkoder.SW
  N5: Mod1.pin_20, TFT_displej.pin_5
  N6: Mod1.pin_22, TFT_displej.pin3
  N7: Mod1.pin_24, TFT_displej.pin_7
  N8: Mod1.pin_25, TFT_displej.pin_6
  N9: Mod1.pin_26, TFT_displej.pin4
  N10: Mod1.pin_27, BMX150_Senzor.SCL
  N11: Mod1.pin_37, TFT_displej.pin_1

custom parts:
  Raspberry Pi Pico W: Raspberry Pi Pico W. Based around the RP2040 microcontroller the Pico W is a low cost microcontroller device bringing Raspberry Pi quality, cost, and easy of use to the microcontroller space. The areas marked KEEPOUT in pcb silkscreen should not have traces running through them to avoid shorts on a soldered in module!
  KY-040 Rotary encoder: KY-040 Rotary Encoder with switch on breakout borad from AZ Delivery
  TFT 1.8 inch 160x128 w SD: This is a generic 1.8 tft spi lcd display available on ebay and others. The 1.8" display has 128x160 color pixels and in this version pin names in breadboard (unlike the real board).
